// Logisim project branch-comp.circ as structural Verilog: 1 circuit, main circuit branch_comp
module branch_comp (
  input  [31:0] BrData1,
  input  [31:0] BrData2,
  input  BrUn,
  output BrEq,
  output BrLt
);

  wire BrEqSigned, BrEqUnsigned, BrLtSigned, BrLtUnsigned;

  Multiplexer multiplexer_1 (.in0(BrEqSigned), .in1(BrEqUnsigned), .out(BrEq), .sel(BrUn));
  Comparator #(.width(32)) comparator_1 (.a(BrData1), .b(BrData2), .eq(BrEqSigned), .lt(BrLtSigned));  // open: gt
  Comparator #(.mode("unsigned"), .width(32)) comparator_2 (
    .a(BrData1), .b(BrData2), .eq(BrEqUnsigned), .lt(BrLtUnsigned));  // open: gt
  Multiplexer multiplexer_2 (.in0(BrLtSigned), .in1(BrLtUnsigned), .out(BrLt), .sel(BrUn));

  // Notes on the sheet:
  //   INPUTS to your circuit
  //   Signed
  //   Unsigned
  //   DON'T CHANGE THE LOCATIONS OF THE INPUTS AND OUTPUTS!
  //   OUTPUT from your circuit
endmodule
