// Logisim project control-logic.circ as structural Verilog: 1 circuit, main circuit control_logic
module control_logic (
  input  [31:0] Instruction,
  input  BrEq,
  input  BrLt,
  output PCSel,
  output RegWEn,
  output [2:0] ImmSel,
  output BrUn,
  output ASel,
  output BSel,
  output [3:0] ALUSel,
  output MemWEn,
  output [1:0] WBSel
);

  wire EqPC, fun3_is_000, fun3_is_001, fun3_is_010, fun3_is_011, fun3_is_100, fun3_is_101, fun3_is_110,
       fun3_is_111, GePC, instr25_is_0, instr25_is_1, instr30_is_0, instr30_is_1, is_add, is_addi, is_and,
       is_andi, is_auipc, is_B_type, is_beq, is_bge, is_bgeu, is_blt, is_bltu, is_bne, is_I_type,
       is_I_type_jalr, is_I_type_load, is_J_type, is_lb, is_lh, is_lui, is_lw, is_mul, is_mulh, is_mulhu,
       is_or, is_ori, is_R_type, is_S_type, is_sb, is_sh, is_sll, is_slli, is_slt, is_slti, is_sra, is_srai,
       is_srl, is_srli, is_sub, is_sw, is_xor, is_xori, JumpPC, LtPC, NePC, not_1_out, not_2_out, or_2_out,
       or_3_out;
  wire [5:0] ROMInput;
  wire [15:14] rom_1_data;

  ROM #(.addrWidth(6), .dataWidth(16)) rom_1 (
    .addr(ROMInput), .data({rom_1_data, WBSel, MemWEn, ALUSel, BSel, ASel, BrUn, ImmSel, RegWEn}));
  or or_1 (PCSel, EqPC, NePC, JumpPC, LtPC, GePC);
  Priority_Encoder #(.select_enc(6)) priority_encoder_1 (
    .in0(is_add), .in1(is_mul), .in2(is_sub), .in3(is_sll), .in4(is_mulh), .in5(is_mulhu), .in6(is_slt),
    .in7(is_xor), .in8(is_srl), .in9(is_sra), .in10(is_or), .in11(is_and), .in12(is_lb), .in13(is_lh),
    .in14(is_lw), .in15(is_addi), .in16(is_slli), .in17(is_slti), .in18(is_xori), .in19(is_srli),
    .in20(is_srai), .in21(is_ori), .in22(is_andi), .in23(is_sb), .in24(is_sh), .in25(is_sw), .in26(is_beq),
    .in27(is_bne), .in28(is_blt), .in29(is_bge), .in30(is_bltu), .in31(is_bgeu), .in32(is_auipc),
    .in33(is_lui), .in34(is_J_type), .in35(is_I_type_jalr), .out(ROMInput));  // open: in36, in37, in38, in39, in40, in41, in42, in43, in44, in45, in46, in47, in48, in49, in50, in51, in52, in53, in54, in55, in56, in57, in58, in59, in60, in61, in62, in63, gs, en_out, en_in
  Comparator #(.width(3)) comparator_1 (.a(Instruction[14:12]), .b(3'b000), .eq(fun3_is_000));  // open: gt, lt
  Comparator #(.width(3)) comparator_2 (.a(Instruction[14:12]), .b(3'b001), .eq(fun3_is_001));  // open: gt, lt
  Comparator #(.width(3)) comparator_3 (.a(Instruction[14:12]), .b(3'b010), .eq(fun3_is_010));  // open: gt, lt
  Comparator #(.width(3)) comparator_4 (.a(Instruction[14:12]), .b(3'b011), .eq(fun3_is_011));  // open: gt, lt
  Comparator #(.width(3)) comparator_5 (.a(Instruction[14:12]), .b(3'b100), .eq(fun3_is_100));  // open: gt, lt
  Comparator #(.width(3)) comparator_6 (.a(Instruction[14:12]), .b(3'b101), .eq(fun3_is_101));  // open: gt, lt
  Comparator #(.width(3)) comparator_7 (.a(Instruction[14:12]), .b(3'b110), .eq(fun3_is_110));  // open: gt, lt
  Comparator #(.width(3)) comparator_8 (.a(Instruction[14:12]), .b(3'b111), .eq(fun3_is_111));  // open: gt, lt
  Comparator #(.width(1)) comparator_9 (.a(Instruction[25]), .b(1'b1), .eq(instr25_is_1));  // open: gt, lt
  Comparator #(.width(1)) comparator_10 (.a(Instruction[25]), .b(1'b0), .eq(instr25_is_0));  // open: gt, lt
  Comparator #(.width(1)) comparator_11 (.a(Instruction[30]), .b(1'b1), .eq(instr30_is_1));  // open: gt, lt
  Comparator #(.width(1)) comparator_12 (.a(Instruction[30]), .b(1'b0), .eq(instr30_is_0));  // open: gt, lt
  not not_1 (not_1_out, BrEq);
  or or_2 (or_2_out, is_blt, is_bltu);
  or or_3 (or_3_out, is_bge, is_bgeu);
  Comparator #(.width(5)) comparator_13 (.a(Instruction[6:2]), .b(5'b11001), .eq(is_I_type_jalr));  // open: gt, lt
  Comparator #(.width(5)) comparator_14 (.a(Instruction[6:2]), .b({5{1'b0}}), .eq(is_I_type_load));  // open: gt, lt
  Comparator #(.width(5)) comparator_15 (.a(Instruction[6:2]), .b(5'b00100), .eq(is_I_type));  // open: gt, lt
  Comparator #(.width(5)) comparator_16 (.a(Instruction[6:2]), .b(5'b01100), .eq(is_R_type));  // open: gt, lt
  Comparator #(.width(5)) comparator_17 (.a(Instruction[6:2]), .b(5'b11000), .eq(is_B_type));  // open: gt, lt
  Comparator #(.width(5)) comparator_18 (.a(Instruction[6:2]), .b(5'b01000), .eq(is_S_type));  // open: gt, lt
  Comparator #(.width(5)) comparator_19 (.a(Instruction[6:2]), .b(5'b11011), .eq(is_J_type));  // open: gt, lt
  Comparator #(.width(5)) comparator_20 (.a(Instruction[6:2]), .b(5'b00101), .eq(is_auipc));  // open: gt, lt
  Comparator #(.width(5)) comparator_21 (.a(Instruction[6:2]), .b(5'b01101), .eq(is_lui));  // open: gt, lt
  and and_1 (EqPC, is_beq, BrEq);
  and and_2 (NePC, is_bne, not_1_out);
  and and_3 (LtPC, or_2_out, BrLt);
  and and_4 (GePC, or_3_out, not_2_out);
  not not_2 (not_2_out, BrLt);
  or or_4 (JumpPC, is_I_type_jalr, is_J_type);
  and and_5 (is_lb, is_I_type_load, fun3_is_000);
  and and_6 (is_lh, is_I_type_load, fun3_is_001);
  and and_7 (is_lw, is_I_type_load, fun3_is_010);
  and and_8 (is_addi, is_I_type, fun3_is_000);
  and and_9 (is_slli, is_I_type, fun3_is_001, instr30_is_0);
  and and_10 (is_slti, is_I_type, fun3_is_010);
  and and_11 (is_xori, is_I_type, fun3_is_100);
  and and_12 (is_srli, is_I_type, fun3_is_101, instr30_is_0);
  and and_13 (is_srai, is_I_type, fun3_is_101, instr30_is_1);
  and and_14 (is_ori, is_I_type, fun3_is_110);
  and and_15 (is_andi, is_I_type, fun3_is_111);
  and and_16 (is_add, is_R_type, fun3_is_000, instr25_is_0, instr30_is_0);
  and and_17 (is_mul, is_R_type, fun3_is_000, instr25_is_1, instr30_is_0);
  and and_18 (is_sub, is_R_type, fun3_is_000, instr25_is_0, instr30_is_1);
  and and_19 (is_sll, is_R_type, fun3_is_001, instr25_is_0);
  and and_20 (is_mulh, is_R_type, fun3_is_001, instr25_is_1);
  and and_21 (is_mulhu, is_R_type, fun3_is_011, instr25_is_1);
  and and_22 (is_slt, is_R_type, fun3_is_010);
  and and_23 (is_xor, is_R_type, fun3_is_100);
  and and_24 (is_srl, is_R_type, fun3_is_101, instr30_is_0);
  and and_25 (is_sra, is_R_type, fun3_is_101, instr30_is_1);
  and and_26 (is_or, is_R_type, fun3_is_110);
  and and_27 (is_and, is_R_type, fun3_is_111);
  and and_28 (is_beq, is_B_type, fun3_is_000);
  and and_29 (is_bne, is_B_type, fun3_is_001);
  and and_30 (is_blt, is_B_type, fun3_is_100);
  and and_31 (is_bge, is_B_type, fun3_is_101);
  and and_32 (is_bltu, is_B_type, fun3_is_110);
  and and_33 (is_bgeu, is_B_type, fun3_is_111);
  and and_34 (is_sb, is_S_type, fun3_is_000);
  and and_35 (is_sh, is_S_type, fun3_is_001);
  and and_36 (is_sw, is_S_type, fun3_is_010);

  // Other names for the same wires on the sheet: opcode[4:0] = Instruction[6:2]; func3[2:0] = Instruction[14:12];
  //   instr25 = Instruction[25]; instr30 = Instruction[30]; is_U_type_auipc = is_auipc; is_jal = is_J_type;
  //   is_jalr = is_I_type_jalr; is_U_type_lui = is_lui

  // Notes on the sheet:
  //   INPUTS to your circuit
  //   contents of rom_1 (hex, n*v repeats v):
  //   1001 1401 1601 1081 1481 1581 1101 1201 1281 1681 1301 1381 2041 2041 2041 1041 10c1 1141 1241 12c1
  //   16c1 1341 13c1 844 844 844 4*62 72 72 1069 17c9 67 41
  //   ROM FOR CONTROL LOGIC
  //   DON'T CHANGE THE LOCATIONS OF THE INPUTS AND OUTPUTS!
  //   This is only if you choose to do the ROM option
  //   OUTPUT from your circuit
  //   Reminder: If using ROM, use combinational logic for PCSel
  //   I type instructions
  //   Jumps instructions
  //   U instructions
  //   R type instructions
  //   B type instructions
  //   S type instructions
endmodule
