// Logisim project cpu.circ as structural Verilog: 1 circuit, main circuit cpu
module cpu (
  input  clk,
  input  [31:0] Instruction,
  input  [31:0] MemReadData,
  output [31:0] MemAddress,
  output [31:0] ProgramCounter,
  output [31:0] ra,
  output [31:0] sp,
  output [31:0] t0,
  output [31:0] t1,
  output [31:0] t2,
  output [31:0] s0,
  output [31:0] s1,
  output [31:0] a0,
  output [3:0] MemWriteMask,
  output [31:0] MemWriteData
);

  wire ASel, BrEq, BrLt, BrUn, BSel, MemWEn, PCSel, RegWEn;
  wire [1:0] WBSel;
  wire [2:0] ImmSel;
  wire [3:0] ALUSel;
  wire [31:0] adder_1_out, adder_2_out, Immediate, Instruction_EX, Instruction_IF, loaded_data,
       multiplexer_1_out, multiplexer_3_out, multiplexer_4_out, PC_EX, rs1Value, rs2Value, WBData;

  Multiplexer #(.width(32)) multiplexer_1 (.in0(adder_1_out), .in1(MemAddress), .out(multiplexer_1_out), .sel(PCSel));
  Register #(.width(32)) PC (.D(multiplexer_1_out), .clk(clk), .Q(ProgramCounter));  // open: en, clr
  Adder #(.width(32)) adder_1 (.a(32'h4), .b(ProgramCounter), .out(adder_1_out));  // open: cin, cout
  Register #(.width(32)) register_1 (.D(ProgramCounter), .clk(clk), .Q(PC_EX));  // open: en, clr
  Register #(.width(32)) register_2 (.D(Instruction_IF), .clk(clk), .Q(Instruction_EX));  // open: en, clr
  Multiplexer #(.width(32)) multiplexer_2 (.in0(Instruction), .in1({32{1'b0}}), .out(Instruction_IF), .sel(PCSel));
  control_logic control_logic_1 (
    .Instruction(Instruction_EX), .BrEq(BrEq), .BrLt(BrLt), .PCSel(PCSel), .RegWEn(RegWEn), .ImmSel(ImmSel),
    .BrUn(BrUn), .ASel(ASel), .BSel(BSel), .ALUSel(ALUSel), .MemWEn(MemWEn), .WBSel(WBSel));
  regfile regfile_1 (
    .ReadIndex1(Instruction_EX[19:15]), .ReadIndex2(Instruction_EX[24:20]),
    .WriteIndex(Instruction_EX[11:7]), .WriteData(WBData), .RegWEn(RegWEn), .clk(clk), .ra(ra), .sp(sp),
    .t0(t0), .t1(t1), .t2(t2), .s0(s0), .s1(s1), .a0(a0), .ReadData1(rs1Value), .ReadData2(rs2Value));
  Multiplexer #(.width(32)) multiplexer_3 (.in0(rs1Value), .in1(PC_EX), .out(multiplexer_3_out), .sel(ASel));
  Multiplexer #(.width(32)) multiplexer_4 (.in0(rs2Value), .in1(Immediate), .out(multiplexer_4_out), .sel(BSel));
  imm_gen imm_gen_1 (.Instruction(Instruction_EX), .ImmSel(ImmSel), .Immediate(Immediate));
  alu alu_1 (.A(multiplexer_3_out), .B(multiplexer_4_out), .ALUSel(ALUSel), .ALUResult(MemAddress));
  Adder #(.width(32)) adder_2 (.a(32'h4), .b(PC_EX), .out(adder_2_out));  // open: cin, cout
  branch_comp branch_comp_1 (.BrData1(rs1Value), .BrData2(rs2Value), .BrUn(BrUn), .BrEq(BrEq), .BrLt(BrLt));
  Multiplexer #(.select(2), .width(32)) multiplexer_5 (
    .in0(adder_2_out), .in1(MemAddress), .in2(loaded_data), .out(WBData), .sel(WBSel));  // open: in3
  partial_store partial_store_1 (
    .Instruction(Instruction_EX), .MemAddress(MemAddress), .DataFromReg(rs2Value), .MemWEn(MemWEn),
    .MemWriteMask(MemWriteMask), .DataToMem(MemWriteData));
  partial_load partial_load_1 (
    .Instruction(Instruction_EX), .MemAddress(MemAddress), .DataFromMem(MemReadData), .DataToReg(loaded_data));

  // Other names for the same wires on the sheet: rdIdx[4:0] = Instruction_EX[11:7];
  //   rs1Idx[4:0] = Instruction_EX[19:15]; rs2Idx[4:0] = Instruction_EX[24:20]; InstrutionFromMem[31:0] = Instruction;
  //   PC_IF[31:0] = ProgramCounter; ALUResult[31:0] = MemAddress; PC_plus_offset[31:0] = MemAddress

  // Notes on the sheet:
  //   To IMEM
  //   IMEM (do **NOT** move this)
  //   From IMEM
  //   Pipline Registers
  //   Deal with control hazards
  //   Inputs/Outputs for testing. Do **NOT** move these.
  //   To DMEM
  //   DMEM (do **NOT** move this)
  //   From DMEM
endmodule
