// Logisim project partial-load.circ as structural Verilog: 1 circuit, main circuit partial_load
module partial_load (
  input  [31:0] Instruction,
  input  [31:0] MemAddress,
  input  [31:0] DataFromMem,
  output [31:0] DataToReg
);

  wire [1:0] Offset, Offset_plus_1;
  wire [7:0] multiplexer_1_out, multiplexer_2_out, multiplexer_3_out;
  wire [31:0] lb_Data, lh_Data;

  Adder #(.width(2)) adder_1 (.a(Offset), .b(2'b01), .out(Offset_plus_1));  // open: cin, cout
  Bit_Extender #(.in_width(32), .out_width(2), .\type ("zero")) bit_extender_1 (.in(MemAddress), .out(Offset));
  assign lb_Data = {{24{multiplexer_1_out[7]}}, multiplexer_1_out};  // Bit_Extender bit_extender_2
  Multiplexer #(.select(2), .width(8)) multiplexer_1 (
    .in0(DataFromMem[7:0]), .in1(DataFromMem[15:8]), .in2(DataFromMem[23:16]), .in3(DataFromMem[31:24]),
    .out(multiplexer_1_out), .sel(Offset));
  Multiplexer #(.select(2), .width(8)) multiplexer_2 (
    .in0(DataFromMem[7:0]), .in1(DataFromMem[15:8]), .in2(DataFromMem[23:16]), .in3(DataFromMem[31:24]),
    .out(multiplexer_2_out), .sel(Offset));
  Multiplexer #(.select(2), .width(8)) multiplexer_3 (
    .in0(DataFromMem[7:0]), .in1(DataFromMem[15:8]), .in2(DataFromMem[23:16]), .in3(DataFromMem[31:24]),
    .out(multiplexer_3_out), .sel(Offset_plus_1));
  assign lh_Data = {{16{multiplexer_3_out[7]}}, {multiplexer_3_out, multiplexer_2_out}};  // Bit_Extender bit_extender_3
  Multiplexer #(.select(3), .width(32)) multiplexer_4 (
    .in0(lb_Data), .in1(lh_Data), .in2(DataFromMem), .out(DataToReg), .sel(Instruction[14:12]));  // open: in3, in4, in5, in6, in7

  // Other names for the same wires on the sheet: func3[2:0] = Instruction[14:12]; lw_Data[31:0] = DataFromMem

  // Notes on the sheet:
  //   INPUTS to your circuit
  //   DON'T CHANGE THE LOCATIONS OF THE INPUTS AND OUTPUTS!
  //   OUTPUT from your circuit
endmodule
