// Logisim project partial-store.circ as structural Verilog: 1 circuit, main circuit partial_store
module partial_store (
  input  [31:0] Instruction,
  input  [31:0] MemAddress,
  input  [31:0] DataFromReg,
  input  MemWEn,
  output [3:0] MemWriteMask,
  output [31:0] DataToMem
);

  wire comparator_1_eq, comparator_2_eq, comparator_3_eq, comparator_4_eq;
  wire [1:0] Offset;
  wire [3:0] bit_extender_2_out, WriteMaskValue;
  wire [31:0] sb_Data, sh_Data;

  Comparator comparator_1 (.a(DataToMem[7:0]), .b({8{1'b0}}), .eq(comparator_1_eq));  // open: gt, lt
  Comparator comparator_2 (.a(DataToMem[15:8]), .b({8{1'b0}}), .eq(comparator_2_eq));  // open: gt, lt
  Comparator comparator_3 (.a(DataToMem[23:16]), .b({8{1'b0}}), .eq(comparator_3_eq));  // open: gt, lt
  Comparator comparator_4 (.a(DataToMem[31:24]), .b({8{1'b0}}), .eq(comparator_4_eq));  // open: gt, lt
  Demultiplexer #(.select(2), .width(8)) demultiplexer_1 (
    .out0(sb_Data[7:0]), .out1(sb_Data[15:8]), .out2(sb_Data[23:16]), .out3(sb_Data[31:24]),
    .in(DataFromReg[7:0]), .sel(Offset));
  Demultiplexer #(.select(2), .width(16)) demultiplexer_2 (
    .out0(sh_Data[15:0]), .out2(sh_Data[31:16]), .in(DataFromReg[15:0]), .sel(Offset));  // open: out1, out3
  not not_1 (WriteMaskValue[0], comparator_1_eq);
  not not_2 (WriteMaskValue[1], comparator_2_eq);
  not not_3 (WriteMaskValue[2], comparator_3_eq);
  not not_4 (WriteMaskValue[3], comparator_4_eq);
  Bit_Extender #(.in_width(32), .out_width(2)) bit_extender_1 (.in(MemAddress), .out(Offset));
  assign bit_extender_2_out = {{3{MemWEn}}, MemWEn};  // Bit_Extender bit_extender_2
  Multiplexer #(.select(3), .width(32)) multiplexer_1 (
    .in0(sb_Data), .in1(sh_Data), .in2(DataFromReg), .out(DataToMem), .sel(Instruction[14:12]));  // open: in3, in4, in5, in6, in7
  assign MemWriteMask = bit_extender_2_out & WriteMaskValue;  // AND_Gate and_1, 4 bits wide

  // Other names for the same wires on the sheet: FirB[7:0] = DataToMem[7:0]; SecB[7:0] = DataToMem[15:8];
  //   ThirB[7:0] = DataToMem[23:16]; FourB[7:0] = DataToMem[31:24]; func3[2:0] = Instruction[14:12];
  //   sw_Data[31:0] = DataFromReg

  // Notes on the sheet:
  //   INPUTS to your circuit
  //   DON'T CHANGE THE LOCATIONS OF THE INPUTS AND OUTPUTS!
  //   OUTPUT from your circuit
endmodule
