// Logisim project regfile.circ as structural Verilog: 1 circuit, main circuit regfile
module regfile (
  input  [4:0] ReadIndex1,
  input  [4:0] ReadIndex2,
  input  [4:0] WriteIndex,
  input  [31:0] WriteData,
  input  RegWEn,
  input  clk,
  output [31:0] ra,
  output [31:0] sp,
  output [31:0] t0,
  output [31:0] t1,
  output [31:0] t2,
  output [31:0] s0,
  output [31:0] s1,
  output [31:0] a0,
  output [31:0] ReadData1,
  output [31:0] ReadData2
);

  wire x0W, x1W, x2W, x3W, x4W, x5W, x6W, x7W, x8W, x9W, x10W, x11W, x12W, x13W, x14W, x15W, x16W, x17W,
       x18W, x19W, x20W, x21W, x22W, x23W, x24W, x25W, x26W, x27W, x28W, x29W, x30W, x31W;
  wire [31:0] x0o, x3o, x4o, x11o, x12o, x13o, x14o, x15o, x16o, x17o, x18o, x19o, x20o, x21o, x22o, x23o,
       x24o, x25o, x26o, x27o, x28o, x29o, x30o, x31o;

  Demultiplexer #(.select(5)) demultiplexer_1 (
    .out0(x0W), .out1(x1W), .out2(x2W), .out3(x3W), .out4(x4W), .out5(x5W), .out6(x6W), .out7(x7W),
    .out8(x8W), .out9(x9W), .out10(x10W), .out11(x11W), .out12(x12W), .out13(x13W), .out14(x14W),
    .out15(x15W), .out16(x16W), .out17(x17W), .out18(x18W), .out19(x19W), .out20(x20W), .out21(x21W),
    .out22(x22W), .out23(x23W), .out24(x24W), .out25(x25W), .out26(x26W), .out27(x27W), .out28(x28W),
    .out29(x29W), .out30(x30W), .out31(x31W), .in(RegWEn), .sel(WriteIndex));
  Multiplexer #(.select(5), .width(32)) multiplexer_1 (
    .in0(x0o), .in1(ra), .in2(sp), .in3(x3o), .in4(x4o), .in5(t0), .in6(t1), .in7(t2), .in8(s0), .in9(s1),
    .in10(a0), .in11(x11o), .in12(x12o), .in13(x13o), .in14(x14o), .in15(x15o), .in16(x16o), .in17(x17o),
    .in18(x18o), .in19(x19o), .in20(x20o), .in21(x21o), .in22(x22o), .in23(x23o), .in24(x24o), .in25(x25o),
    .in26(x26o), .in27(x27o), .in28(x28o), .in29(x29o), .in30(x30o), .in31(x31o), .out(ReadData1),
    .sel(ReadIndex1));
  Multiplexer #(.select(5), .width(32)) multiplexer_2 (
    .in0(x0o), .in1(ra), .in2(sp), .in3(x3o), .in4(x4o), .in5(t0), .in6(t1), .in7(t2), .in8(s0), .in9(s1),
    .in10(a0), .in11(x11o), .in12(x12o), .in13(x13o), .in14(x14o), .in15(x15o), .in16(x16o), .in17(x17o),
    .in18(x18o), .in19(x19o), .in20(x20o), .in21(x21o), .in22(x22o), .in23(x23o), .in24(x24o), .in25(x25o),
    .in26(x26o), .in27(x27o), .in28(x28o), .in29(x29o), .in30(x30o), .in31(x31o), .out(ReadData2),
    .sel(ReadIndex2));
  Register #(.width(32)) x0 (.D({32{1'b0}}), .en(x0W), .clk(clk), .Q(x0o));  // open: clr
  Register #(.width(32)) x1_ra (.D(WriteData), .en(x1W), .clk(clk), .Q(ra));  // open: clr
  Register #(.width(32)) x2_sp (.D(WriteData), .en(x2W), .clk(clk), .Q(sp));  // open: clr
  Register #(.width(32)) x3_gp (.D(WriteData), .en(x3W), .clk(clk), .Q(x3o));  // open: clr
  Register #(.width(32)) x4_tp (.D(WriteData), .en(x4W), .clk(clk), .Q(x4o));  // open: clr
  Register #(.width(32)) x5_t0 (.D(WriteData), .en(x5W), .clk(clk), .Q(t0));  // open: clr
  Register #(.width(32)) x6_t1 (.D(WriteData), .en(x6W), .clk(clk), .Q(t1));  // open: clr
  Register #(.width(32)) x7_t2 (.D(WriteData), .en(x7W), .clk(clk), .Q(t2));  // open: clr
  Register #(.width(32)) x8_s0 (.D(WriteData), .en(x8W), .clk(clk), .Q(s0));  // open: clr
  Register #(.width(32)) x9_s1 (.D(WriteData), .en(x9W), .clk(clk), .Q(s1));  // open: clr
  Register #(.width(32)) x10_a0 (.D(WriteData), .en(x10W), .clk(clk), .Q(a0));  // open: clr
  Register #(.width(32)) x11_a1 (.D(WriteData), .en(x11W), .clk(clk), .Q(x11o));  // open: clr
  Register #(.width(32)) x12_a2 (.D(WriteData), .en(x12W), .clk(clk), .Q(x12o));  // open: clr
  Register #(.width(32)) x13_a3 (.D(WriteData), .en(x13W), .clk(clk), .Q(x13o));  // open: clr
  Register #(.width(32)) x14_a4 (.D(WriteData), .en(x14W), .clk(clk), .Q(x14o));  // open: clr
  Register #(.width(32)) x15_a5 (.D(WriteData), .en(x15W), .clk(clk), .Q(x15o));  // open: clr
  Register #(.width(32)) x16_a6 (.D(WriteData), .en(x16W), .clk(clk), .Q(x16o));  // open: clr
  Register #(.width(32)) x17_a7 (.D(WriteData), .en(x17W), .clk(clk), .Q(x17o));  // open: clr
  Register #(.width(32)) x18_s2 (.D(WriteData), .en(x18W), .clk(clk), .Q(x18o));  // open: clr
  Register #(.width(32)) x19_s3 (.D(WriteData), .en(x19W), .clk(clk), .Q(x19o));  // open: clr
  Register #(.width(32)) x20_s4 (.D(WriteData), .en(x20W), .clk(clk), .Q(x20o));  // open: clr
  Register #(.width(32)) x21_s5 (.D(WriteData), .en(x21W), .clk(clk), .Q(x21o));  // open: clr
  Register #(.width(32)) x22_s6 (.D(WriteData), .en(x22W), .clk(clk), .Q(x22o));  // open: clr
  Register #(.width(32)) x23_s7 (.D(WriteData), .en(x23W), .clk(clk), .Q(x23o));  // open: clr
  Register #(.width(32)) x24_s8 (.D(WriteData), .en(x24W), .clk(clk), .Q(x24o));  // open: clr
  Register #(.width(32)) x25_s9 (.D(WriteData), .en(x25W), .clk(clk), .Q(x25o));  // open: clr
  Register #(.width(32)) x26_s10 (.D(WriteData), .en(x26W), .clk(clk), .Q(x26o));  // open: clr
  Register #(.width(32)) x27_s11 (.D(WriteData), .en(x27W), .clk(clk), .Q(x27o));  // open: clr
  Register #(.width(32)) x28_t3 (.D(WriteData), .en(x28W), .clk(clk), .Q(x28o));  // open: clr
  Register #(.width(32)) x29_t4 (.D(WriteData), .en(x29W), .clk(clk), .Q(x29o));  // open: clr
  Register #(.width(32)) x30_t5 (.D(WriteData), .en(x30W), .clk(clk), .Q(x30o));  // open: clr
  Register #(.width(32)) t31_t6 (.D(WriteData), .en(x31W), .clk(clk), .Q(x31o));  // open: clr

  // Other names for the same wires on the sheet: x1o[31:0] = ra; x2o[31:0] = sp; x5o[31:0] = t0; x6o[31:0] = t1;
  //   x7o[31:0] = t2; x8o[31:0] = s0; x9o[31:0] = s1; x10o[31:0] = a0

  // Notes on the sheet:
  //   INPUTS to your circuit
  //   DON'T CHANGE THE LOCATIONS OF THE INPUTS AND OUTPUTS!
  //   These are DEBUG/TEST outputs from your circuit.
  //   OUTPUTS from your circuit
  //   32 Registers!
endmodule
