// Logisim project bne.circ as structural Verilog: 1 circuit, main circuit run_main
module run_main (
  output [31:0] ra,
  output [31:0] sp,
  output [31:0] t0,
  output [31:0] t1,
  output [31:0] t2,
  output [31:0] s0,
  output [31:0] s1,
  output [31:0] a0,
  output [31:0] RequestedAddress,
  output [31:0] RequestedInstruction,
  output [15:0] TimeStep,
  output halt
);

  wire clk;

  Clock clock_1 (.out(clk));
  // Probe on RequestedAddress
  // cpu_harness cpu_harness_1: pin names not known; wires that end beside it: RequestedInstruction, clk, RequestedAddress, ra, sp, t0, t1, t2, s0, s1, a0
  ROM #(.addrWidth(14), .dataWidth(32)) rom_1 (.addr(RequestedAddress[15:2]), .data(RequestedInstruction));
  // Probe on RequestedInstruction
  Counter #(.max('hffff), .width(16)) counter_1 (.clk(clk), .Q(TimeStep));  // open: clr, load, up, count, D, carry
  Comparator #(.width(16)) comparator_1 (.a(TimeStep), .b(16'h48), .eq(halt));  // open: gt, lt

  // Other names for the same wires on the sheet: Instruction[31:0] = RequestedInstruction;
  //   ProgramCounter[31:0] = RequestedAddress

  // Notes on the sheet:
  //   contents of rom_1 (hex, n*v repeats v):
  //   433 4b3 3b3 e00293 3ff00313 629863 700413 ff600493 409403b3 2528633 1960613 433 4b3 3b3 fe900293
  //   1700313 629663 900413 c00493 b00913 433 4b3 3b3 1c00293 1c00313 629a63 900413 300493 84a3b3 29383b3
  //   c00913 433 4b3 3b3 80100293 80000313 629a63 200513 7d000413 a414b3 29413b3 fec00913 200513 40a95933
  //   433 4b3 3b3 c8800293 c8800313 629a63 ffb00413 83000493 29433b3 2949433 80800913 194913 433 4b3 3b3
  //   2b3 100313 629863 400413 800493 a00393 ffd00913 1f01913 433 4b3 3b3 2b3 333 629a63 c00413 ffb00493
  //   1e00393 4074d4b3 6300393
  //   Instruction Memory
  //   Halts Execution After Constant # of Clock Cycles
  //   Constant
endmodule
